# Fritzing sketch CO Sensor (saved by Fritzing 0.9.9b)

parts:
  MCU1 = Wemos Lolin32lite
  Squix1 = OLED 0.96" 128x64 I2C SSD1306
  M1 = BME280
  Grove1 = Grove 3 Axis Digital Accelerometer 16g
  J1 = Piezo Speaker

nets:
  N1: MCU1.pin_6, Squix1.SCA, M1.SDA, Grove1.SCL
  N2: MCU1.pin_7, Squix1.SCL, M1.SCL, Grove1.SDA
  N3: MCU1.pin_8, J1.pin2
  VCC: MCU1.pin_28, Squix1.VCC, M1.VIN, Grove1.VCC
  GND: Squix1.GND, M1.GND
  N4: Grove1.GND, J1.pin1

notes:
  OLED SCREEN
  BME280
  Lolin32 lite
  BUZER
  Multi Gas Sencor

custom parts:
  Wemos Lolin32lite: Wemos Lolinlite32 wifi and blue tooth board based on the ESP-32 cpu, digital I/Os 19, analog inputs 6, clock 240mhz, Flash 4Mbytes, lipo battery charger (500ma connection broken out on breadboard but not pcb), usb.
  BME280: Temperature Humidity Barometric presure Sensor
