# Fritzing sketch Czujnik CO (saved by Fritzing 0.9.3b)

parts:
  Czujnik3 = BME280 Breakout
  WeMos_D1_Mini3 = WeMos D1 Mini
  ZS-042_RTC2 = ZS-042 RTC Module  # not connected
  F2 = Fan - Ventilador [package=THT]
  U6 = 2-Channel 5v Relay Shield [package=relay-2ch5v10a]
  R2 = Resistor [tolerance=±5% resistance=360 package=THT]
  TRANSIL = Schottky Diode [part_number=12V package="300 mil [THT]"]
  EL817 = TLP621 [package=THT]
  Cewka_Pieca_CO = Inductor [package="1206 [SMD]"]
  R1 = Resistor [tolerance=±5% resistance=10k package=THT]
  J1 = Piezo Speaker
  OLED_I2C2 = OLED 128x64 I2C Monochrome Display  # not connected

nets:
  N1: Czujnik3.GND, WeMos_D1_Mini3.G
  3.3V: Czujnik3.3.3V, WeMos_D1_Mini3.3V3
  N2: Czujnik3.SDI/SDA, WeMos_D1_Mini3.D2
  N3: Czujnik3.SCK/SCL, WeMos_D1_Mini3.D1
  N4: WeMos_D1_Mini3.D5, U6.GND, U6.IN1
  N5: WeMos_D1_Mini3.D6, J1.pin2
  N6: WeMos_D1_Mini3.D7, EL817.Pin_4, R1.Pin_1
  N7: F2.GND, U6.K1-On
  N8: R2.Pin_0, EL817.Pin_1
  N9: R2.Pin_1, TRANSIL.cathode, Cewka_Pieca_CO.pin_0
  N10: TRANSIL.anode, EL817.Pin_2, Cewka_Pieca_CO.pin_1

notes:
  Łazienka Rodziców CO & FAN
  Wemos D1 PRO
  BME280
  Multigas sensor
  N
  L
  Wentylator
  Przekaźniki
  Odczyt działania Kotła CO
  +10V
  OLED 0,96"
  128x64
  BUZER

custom parts:
  Fan - Ventilador: Ventilador de 2 pines, se encuentra comunmente en computadoras de escritorio
  2-Channel 5v Relay Shield: 2 Channel 5v Relay Shield w. 2x SPD-06VDC-SD-C

// code stored in the sketch: ESP8266-BME280-Blynk.ino


//Example>Blynk>BoardAndShield>ESP8266StandAlone

//

/**************************************************************

* Blynk is a platform with iOS and Android apps to control

* Arduino, Raspberry Pi and the likes over the Internet.

* You can easily build graphic interfaces for all your

* projects by simply dragging and dropping widgets.

*

* Downloads, docs, tutorials: http://www.blynk.cc

* Blynk community: http://community.blynk.cc

* Social networks: http://www.fb.com/Blynkapp

* http://twitter.com/blynk_app

*

* Blynk library is licensed under MIT license

* This example code is in public domain.

*

**************************************************************

* This example runs directly on ESP8266 chip.

*

* You need to install this for ESP8266 development:

* https://github.com/esp8266/Arduino

* 

* Please be sure to select hte right ESP8266 module

* in the Tools -> Board menu!

*

* Change WiFi ssid, pass, and Blynk auth token to run :)

*

**************************************************************/

//Pragmas

//#define BLYNK_PRINT Serial // Comment this out to disable prints and save space

//#define BLYNK_DEBUG //For debug



//Include Headers

#include <ESP8266WiFi.h>

#include <BlynkSimpleEsp8266.h>

#include <BME280_MOD-1022.h>

#include <Wire.h>



// You should get Auth Token in the Blynk App.

// Go to the Project Settings (nut icon).

char auth[] = "*************";



unsigned long lastCheck = 0;

double tempMostAccurate, humidityMostAccurate, pressureMostAccurate;

char buff[50];



// Arduino needs this to bring pretty numbers

void printFormattedFloat(float x, uint8_t precision) {

char buffer[10];

dtostrf(x, 7, precision, buffer);

Serial.print(buffer);

}

void formattedFloat(float x, uint8_t precision, char *buff) {

dtostrf(x, 7, precision, buff);

}



void setup()

{

Serial.begin(115200);

#ifdef BLYNK_DEBUG

Serial.println("");

Serial.println("Begin Serial");

#endif

Blynk.begin(auth, "ssid", "password");//ssid,pass

#ifdef BLYNK_DEBUG

Serial.println("Begin Wifi");

Serial.println("Begin BME280");

#endif

Wire.begin();

pinMode(12,OUTPUT);



//BME280 Setup

// need to read the NVM compensation parameters

BME280.readCompensationParams();

BME280.writeStandbyTime(tsb_0p5ms); // tsb = 0.5ms

BME280.writeFilterCoefficient(fc_16); // IIR Filter coefficient 16

BME280.writeOversamplingPressure(os16x); // pressure x16

BME280.writeOversamplingTemperature(os2x); // temperature x2

BME280.writeOversamplingHumidity(os1x); // humidity x1

BME280.writeMode(smNormal);



}



BLYNK_READ(V0)

{

tempMostAccurate = BME280.getTemperatureMostAccurate();

#ifdef BLYNK_DEBUG

//Serial.print("Temp ");

//printFormattedFloat(tempMostAccurate, 2);

//Serial.println();

#endif

char buff1[50];

formattedFloat(tempMostAccurate, 2, buff1);

Blynk.virtualWrite(V0, buff1);

}



BLYNK_READ(V1)

{

humidityMostAccurate = BME280.getHumidityMostAccurate();

#ifdef BLYNK_DEBUG

//Serial.print("humid ");

//printFormattedFloat(humidityMostAccurate, 2);

//Serial.println();

#endif

char buf[6];

dtostrf(humidityMostAccurate,3,2,buf);

Blynk.virtualWrite(V1, String(buf));

}



BLYNK_READ(V2)

{

pressureMostAccurate = BME280.getPressureMostAccurate();

#ifdef BLYNK_DEBUG

//Serial.print("pressure ");

//printFormattedFloat(pressureMostAccurate, 2);

//Serial.println();

#endif

char buf8[8];

// formattedFloat(pressureMostAccurate, 2, buff);

dtostrf(pressureMostAccurate,5,2,buf8);

Blynk.virtualWrite(V2, String(buf8));

}





void loop()

{

Blynk.run();



int diff = millis() - lastCheck;

if (diff > 1000) {

while (BME280.isMeasuring()) {

}

// read out the data - must do this before calling the getxxxxx routines

BME280.readMeasurements();



//For Debugging, Serial Print Temp+Humid+Pressure

#ifdef BLYNK_DEBUG

tempMostAccurate = BME280.getTemperatureMostAccurate();

Serial.print("Temp:");

printFormattedFloat(tempMostAccurate, 2); 

humidityMostAccurate = BME280.getHumidityMostAccurate();

Serial.print(" Humid:");

printFormattedFloat(humidityMostAccurate, 2);

pressureMostAccurate = BME280.getPressureMostAccurate();

Serial.print(" Pressure:");

printFormattedFloat(pressureMostAccurate, 2);

Serial.println();

#endif



lastCheck = millis();

} else if (diff < 0) {

lastCheck = 0;

}

}
