# Fritzing sketch Automatyczne podlewanie (saved by Fritzing 0.9.3b)

parts:
  Capacitive_Sol_Moisture_Sensor_V1_4 = Capacitive Sol Moisture Sensor V1.0
  Capacitive_Sol_Moisture_Sensor_V1_5 = Capacitive Sol Moisture Sensor V1.0
  VCC2 = Battery
  M5 = DC Motor
  M6 = DC Motor
  2_Channel_Relay1 = 2 Channel Power Relay
  U7 = NodeMCU V3.0
  X1 = USB Connectors [package=usb-microb]

nets:
  N1: Capacitive_Sol_Moisture_Sensor_V1_4.A, Capacitive_Sol_Moisture_Sensor_V1_5.A, U7.A0
  N2: Capacitive_Sol_Moisture_Sensor_V1_4.VCC, U7.D1
  GND: Capacitive_Sol_Moisture_Sensor_V1_4.GND, Capacitive_Sol_Moisture_Sensor_V1_5.GND, U7.RSV
  N3: Capacitive_Sol_Moisture_Sensor_V1_5.VCC, U7.D2
  N4: VCC2.-, X1.GND
  N5: VCC2.+, M5.pin_2, M6.pin_2, X1.VBUS
  N6: M5.pin_1, 2_Channel_Relay1.K1-NO
  N7: M6.pin_1, 2_Channel_Relay1.K2-NO
  GND_2: 2_Channel_Relay1.GND, U7.GND
  N8: 2_Channel_Relay1.IN1, U7.D5
  N9: 2_Channel_Relay1.IN2, U7.D6
  VCC: 2_Channel_Relay1.VCC, U7.3V3
  N10: U7.D0, U7.RST

notes:
  Czujnik A
  D1
  Czujnik B
  D2
  Pompa A
  Pompa B
  System Podlewania
  Power 5V

custom parts:
  Capacitive Sol Moisture Sensor V1.0: Soild moisture sensor developed by DFROBOT. It is resistant to corrosion.
  Battery: Your standard 2x 18650 battery pack (7,4 Volts)
  2 Channel Power Relay: A 2 channel power relay. The module operates at 5V.
  NodeMCU V3.0: NodeMcu V3 Lua WIFI Development Board
