# Fritzing sketch ESP32 Pokoj Rymanowska (saved by Fritzing 0.9.4)

parts:
  M2 = BME280
  MCU1 = Wemos Lolin32lite
  TFT2 = Color 320x240 TFT Display, ILI9341 Controller Chip  # not connected
  U1 = PIC-ICSP [part_number=ST7789 package=molex-1x6]
  R1 = Resistor [tolerance=±5% resistance=4.7k package=THT]
  DS1 = DS18B20 1-Wire Temperature Sensor [part_number=DS18B20]
  S3 = Pushbutton [package="[SMD]"]

nets:
  VIN: M2.VIN, MCU1.pin_28, U1.PGC, R1.Pin_0, DS1.VDD
  GND: M2.GND, MCU1.pin_13, U1.PGM, DS1.GND, S3.Pin_3, S3.Pin_4
  N1: M2.SCL, MCU1.pin_6
  N2: M2.SDA, MCU1.pin_7
  N3: MCU1.pin_4, S3.Pin_1
  N4: MCU1.pin_16, R1.Pin_1, DS1.DQ
  N5: MCU1.pin_20, U1.VCC
  N6: MCU1.pin_22, U1.VPP
  N7: MCU1.pin_24, U1.PGD
  N8: MCU1.pin_25, U1.GND

notes:
  Piny ST7789
  SHT31

custom parts:
  BME280: Temperature Humidity Barometric presure Sensor
  Wemos Lolin32lite: Wemos Lolinlite32 wifi and blue tooth board based on the ESP-32 cpu, digital I/Os 19, analog inputs 6, clock 240mhz, Flash 4Mbytes, lipo battery charger (500ma connection broken out on breadboard but not pcb), usb.
  Color 320x240 TFT Display, ILI9341 Controller Chip: 2.2" TFT Display with ILI9341 Controller
