# Fritzing sketch Wine_Temp_Regulator (saved by Fritzing 0.9.9b)

parts:
  DS1 = DS18B20 1-Wire Temperature Sensor [part_number=1B]
  DS2 = DS18B20 1-Wire Temperature Sensor [part_number=2B]
  DS3 = DS18B20 1-Wire Temperature Sensor [part_number=3B]
  DS4 = DS18B20 1-Wire Temperature Sensor [part_number=4B]
  MCU1 = Wemos Lolin32lite
  R1 = Resistor [tolerance=±5% power=0.25 resistance=4.7k package=THT]
  Power_plug1 = Power plug [part_number="Zasilanie 240V"]
  M1 = 4 way omron relay module
  S2 = Textile Pushbutton [part_number="WINO #2 HEAT MAT"]
  S3 = Textile Pushbutton [part_number="WINO #4 HEAT MAT"]
  S4 = Textile Pushbutton [part_number="WINO #3 HEAT MAT"]
  S1 = Textile Pushbutton [part_number="WINO #1 HEAT MAT"]
  M2 = BME280 [part_number=SHT31]
  DS5 = DS18B20 1-Wire Temperature Sensor [part_number=1A]
  DS6 = DS18B20 1-Wire Temperature Sensor [part_number=2A]
  DS7 = DS18B20 1-Wire Temperature Sensor [part_number=3A]
  DS8 = DS18B20 1-Wire Temperature Sensor [part_number=4A]

nets:
  VDD: DS1.VDD, DS2.VDD, DS3.VDD, DS4.VDD, MCU1.pin_28, R1.Pin_0, M1.DC+, M2.VIN
  N1: DS1.DQ, DS2.DQ, DS3.DQ, DS4.DQ, MCU1.pin_20, R1.Pin_1
  GND: DS1.GND, DS2.GND, DS3.GND, DS4.GND, MCU1.pin_13, M1.DC-, M2.GND
  N2: MCU1.pin_5, M1.CH1
  N3: MCU1.pin_6, M2.SCL
  N4: MCU1.pin_7, M2.SDA
  N5: MCU1.pin_8, M1.CH2
  N6: MCU1.pin_9, M1.CH3
  N7: MCU1.pin_10, M1.CH4
  N8: Power_plug1.GND, M1.N4, M1.N3, M1.N2, M1.N1
  N9: Power_plug1.VCC, S2.leg0, S3.leg0, S4.leg0, S1.leg0
  N10: M1.L4, S3.leg1
  N11: M1.L3, S4.leg1
  N12: M1.L2, S2.leg1
  N13: M1.L1, S1.leg1
  VDD_2: DS5.VDD, DS6.VDD, DS7.VDD, DS8.VDD
  N14: DS5.DQ, DS6.DQ, DS7.DQ, DS8.DQ
  GND_2: DS5.GND, DS6.GND, DS7.GND, DS8.GND

custom parts:
  Wemos Lolin32lite: Wemos Lolinlite32 wifi and blue tooth board based on the ESP-32 cpu, digital I/Os 19, analog inputs 6, clock 240mhz, Flash 4Mbytes, lipo battery charger (500ma connection broken out on breadboard but not pcb), usb.
  4 way omron relay module: Low Level 5V 4 Channel Solid State Relay Module SSR G3MB-202P 240V 2A Output with Resistive Fuse.
  BME280: Temperature Humidity Barometric presure Sensor
